// Logisim project MULTIPROCESSOR DEMONSTRATION.circ as structural Verilog: 10 circuits, main circuit main
module main (
  input  CLEAR,
  output [7:0] out_2,
  output [3:0] out_3
);

  wire clock_1_out, register_file_1_out_12;
  wire [3:0] multiplexer_1_out;
  wire [6:0] register_file_1_out_5;
  wire [7:0] counter_1_q, rom_2_data;

  Clock clock_1 (.out(clock_1_out));
  Counter counter_1 (.Q(counter_1_q), .clk(clock_1_out), .clr(CLEAR));  // open: load, D, count, carry
  ROM rom_1 (.addr(counter_1_q), .data(out_2));  // open: sel
  Multiplexer #(.width(4), .enable("false")) multiplexer_1 (
    .in0(out_2[3:0]), .in1(out_3), .out(multiplexer_1_out), .sel(rom_2_data[3]));
  ROM #(.addrWidth(4)) rom_2 (.addr(out_2[7:4]), .data(rom_2_data));  // open: sel
  register_file register_file_1 (
    .MUX_INPUT(multiplexer_1_out), .WE(rom_2_data[0]), .ADDER(rom_2_data[1]), .CLOCK(clock_1_out),
    .out_5(register_file_1_out_5[0]), .out_6(register_file_1_out_5[1]), .out_7(register_file_1_out_5[2]),
    .out_8(register_file_1_out_5[3]), .out_9(register_file_1_out_5[4]), .out_10(register_file_1_out_5[5]),
    .out_11(register_file_1_out_5[6]), .out_12(register_file_1_out_12));
  alu alu_1 (
    .A0(register_file_1_out_5[0]), .A1(register_file_1_out_5[1]), .A2(register_file_1_out_5[2]),
    .A3(register_file_1_out_5[3]), .B0(register_file_1_out_5[4]), .B1(register_file_1_out_5[5]),
    .B2(register_file_1_out_5[6]), .B3(register_file_1_out_12), .HARDWARE_SUBTRACT(rom_2_data[7]),
    .S0(rom_2_data[5]), .S1(rom_2_data[6]), .CLOCK(clock_1_out), .LOAD(rom_2_data[4]), .out_14(out_3));
  TTY tty_1 (.data(register_file_1_out_5), .clk(clock_1_out), .we(rom_2_data[2]), .clr(CLEAR));

  // Notes on the sheet:
  //   CLOCK
  //   COUNTER
  //   PROM
  //   contents of rom_1 (hex, n*v repeats v):
  //   0 18 24 30 15 26 30 1c 26 30 30 1f 26 30 1c 22 30 10 22 30 12 24 30 14 24 30 1a 20 30 13 23 30 1b 22
  //   30 14 23 30 1d 23 30 13 24 60 40 23 30 1a 20 30 13 23 30 1a 22 30 13 23 30 1d 23 30 13 23 60 40 60
  //   40 30 1d 20 30 14 23 30 1d 22 30 13 23 30 1d 23 30 13 2f 90 40 21 60 40 24 60 40 23 30 1a 20 30 14
  //   23 30 1d 22 30 13 23 30 1d 23 30 10 20 60 14 23 a0 40 23 30 1a 20 30
  //   INSTRUCTION DECODER
  //   contents of rom_2 (hex, n*v repeats v):
  //   0 1 3 4 9 b 10 30 50 70 90
  //   REGISTER FILE
  //   ALU
  //   DISPLAY
endmodule

module _1_bit_circuit (
  input  D,
  input  LOAD,
  input  CLOCK,
  output out_4
);

  wire multiplexer_1_out;

  Multiplexer #(.enable("false")) multiplexer_1 (.in0(out_4), .in1(D), .out(multiplexer_1_out), .sel(LOAD));
  D_Flip_Flop d_ff_1 (.clk(CLOCK), .D(multiplexer_1_out), .Q(out_4));  // open: Qn, preset, en, reset

  // Notes on the sheet:
  //   1-BIT REGISTER
endmodule

module _4_bit_register (
  input  A0,
  input  A1,
  input  A2,
  input  A3,
  input  CLOCK,
  input  LOAD,
  output out_7,
  output out_8,
  output out_9,
  output out_10
);

  _1_bit_circuit u_1_bit_circuit_1 (.D(A0), .CLOCK(CLOCK), .out_4(out_7), .LOAD(LOAD));
  _1_bit_circuit u_1_bit_circuit_2 (.D(A1), .CLOCK(CLOCK), .out_4(out_8), .LOAD(LOAD));
  _1_bit_circuit u_1_bit_circuit_3 (.D(A2), .CLOCK(CLOCK), .out_4(out_9), .LOAD(LOAD));
  _1_bit_circuit u_1_bit_circuit_4 (.D(A3), .CLOCK(CLOCK), .out_4(out_10), .LOAD(LOAD));

  // Notes on the sheet:
  //   4-BIT REGISTER
endmodule

module register_file (
  input  [3:0] MUX_INPUT,
  input  WE,
  input  ADDER,
  input  CLOCK,
  output out_5,
  output out_6,
  output out_7,
  output out_8,
  output out_9,
  output out_10,
  output out_11,
  output out_12
);

  wire and_1_out, and_2_out, not_1_out;

  not not_1 (not_1_out, ADDER);
  and and_1 (and_1_out, WE, not_1_out);
  and and_2 (and_2_out, WE, ADDER);
  _4_bit_register u_4_bit_register_1 (
    .A0(MUX_INPUT[0]), .A1(MUX_INPUT[1]), .A2(MUX_INPUT[2]), .A3(MUX_INPUT[3]), .out_7(out_5), .out_8(out_6),
    .out_9(out_7), .out_10(out_8), .LOAD(and_1_out), .CLOCK(CLOCK));
  _4_bit_register u_4_bit_register_2 (
    .A0(MUX_INPUT[0]), .A1(MUX_INPUT[1]), .A2(MUX_INPUT[2]), .A3(MUX_INPUT[3]), .out_7(out_9),
    .out_8(out_10), .out_9(out_11), .out_10(out_12), .LOAD(and_2_out), .CLOCK(CLOCK));

  // Notes on the sheet:
  //   REGISTER 0
  //   REGISTER 1
  //   REGISTER FILE
endmodule

module alu (
  input  HARDWARE_SUBTRACT,
  input  A0,
  input  A1,
  input  A2,
  input  A3,
  input  B0,
  input  B1,
  input  B2,
  input  B3,
  input  CLOCK,
  input  LOAD,
  input  S0,
  input  S1,
  output [3:0] out_14
);

  wire adder_1_out_10, adder_1_out_11, adder_1_out_12, adder_1_out_13, and_1_out_9, and_1_out_10,
       and_1_out_11, and_1_out_12, multiplexer_1_out, multiplexer_2_out, multiplexer_3_out,
       multiplexer_4_out, or_1_out_9, or_1_out_10, or_1_out_11, or_1_out_12, xor_1_out_9, xor_1_out_10,
       xor_1_out_11, xor_1_out_12;

  adder adder_1 (
    .A0(A0), .A1(A1), .A2(A2), .A3(A3), .in_5(HARDWARE_SUBTRACT), .B0(B0), .B1(B1), .B2(B2), .B3(B3),
    .out_10(adder_1_out_10), .out_11(adder_1_out_11), .out_12(adder_1_out_12), .out_13(adder_1_out_13));
  \or  or_1 (
    .A0(A0), .A1(A1), .A2(A2), .A3(A3), .B0(B0), .B1(B1), .B2(B2), .B3(B3), .out_9(or_1_out_9),
    .out_10(or_1_out_10), .out_11(or_1_out_11), .out_12(or_1_out_12));
  \and  and_1 (
    .A0(A0), .A1(A1), .A2(A2), .A3(A3), .B0(B0), .B1(B1), .B2(B2), .in_8(B3), .out_9(and_1_out_9),
    .out_10(and_1_out_10), .out_11(and_1_out_11), .out_12(and_1_out_12));
  \xor  xor_1 (
    .A0(A0), .A1(A1), .A2(A2), .A3(A3), .B0(B0), .B1(B1), .B2(B2), .B3(B3), .out_9(xor_1_out_9),
    .out_10(xor_1_out_10), .out_11(xor_1_out_11), .out_12(xor_1_out_12));
  Multiplexer #(.select(2), .enable("false")) multiplexer_1 (
    .in0(adder_1_out_10), .in1(or_1_out_9), .in2(and_1_out_9), .in3(xor_1_out_9), .out(multiplexer_1_out),
    .sel({S0, S1}));
  Multiplexer #(.select(2), .enable("false")) multiplexer_2 (
    .in0(adder_1_out_11), .in1(or_1_out_10), .in2(and_1_out_10), .in3(xor_1_out_10), .out(multiplexer_2_out),
    .sel({S0, S1}));
  Multiplexer #(.select(2), .enable("false")) multiplexer_3 (
    .in0(adder_1_out_12), .in1(or_1_out_11), .in2(and_1_out_11), .in3(xor_1_out_11), .out(multiplexer_3_out),
    .sel({S0, S1}));
  Multiplexer #(.select(2), .enable("false")) multiplexer_4 (
    .in0(adder_1_out_13), .in1(or_1_out_12), .in2(and_1_out_12), .in3(xor_1_out_12), .out(multiplexer_4_out),
    .sel({S0, S1}));
  _4_bit_register u_4_bit_register_1 (
    .A0(multiplexer_1_out), .A1(multiplexer_2_out), .A2(multiplexer_3_out), .A3(multiplexer_4_out),
    .out_7(out_14[0]), .out_8(out_14[1]), .out_9(out_14[2]), .out_10(out_14[3]), .LOAD(LOAD), .CLOCK(CLOCK));

  // Notes on the sheet:
  //   ALU
  //   ACCUMULATER
endmodule

// ADDER
module adder (
  input  A0,
  input  A1,
  input  A2,
  input  A3,
  input  in_5,
  input  B0,
  input  B1,
  input  B2,
  input  B3,
  output out_10,
  output out_11,
  output out_12,
  output out_13
);

  wire n1_bit_full_adder_1_co, n1_bit_full_adder_2_co, n1_bit_full_adder_3_co, n1_bit_full_adder_4_co,
       xor_1_out, xor_2_out, xor_3_out, xor_4_out;

  xor xor_1 (xor_1_out, in_5, B0);
  xor xor_2 (xor_2_out, in_5, B1);
  xor xor_3 (xor_3_out, in_5, B2);
  xor xor_4 (xor_4_out, in_5, B3);
  _1_bit_full_adder u_1_bit_full_adder_1 (.A(A0), .B(xor_1_out), .C(in_5), .S(out_10), .CO(n1_bit_full_adder_1_co));
  _1_bit_full_adder u_1_bit_full_adder_2 (
    .A(A1), .B(xor_2_out), .C(n1_bit_full_adder_1_co), .S(out_11), .CO(n1_bit_full_adder_2_co));
  _1_bit_full_adder u_1_bit_full_adder_3 (
    .A(A2), .B(xor_3_out), .C(n1_bit_full_adder_2_co), .S(out_12), .CO(n1_bit_full_adder_3_co));
  _1_bit_full_adder u_1_bit_full_adder_4 (
    .A(A3), .B(xor_4_out), .C(n1_bit_full_adder_3_co), .S(out_13), .CO(n1_bit_full_adder_4_co));
  // also tied to GND on the sheet: n1_bit_full_adder_4_co

  // Notes on the sheet:
  //   ADDER
endmodule

// OR
module \or  (
  input  A0,
  input  A1,
  input  A2,
  input  A3,
  input  B0,
  input  B1,
  input  B2,
  input  B3,
  output out_9,
  output out_10,
  output out_11,
  output out_12
);

  or or_1 (out_9, A0, B0);
  or or_2 (out_10, A1, B1);
  or or_3 (out_11, A2, B2);
  or or_4 (out_12, A3, B3);

  // Notes on the sheet:
  //   OR
endmodule

// AND
module \and  (
  input  A0,
  input  A1,
  input  A2,
  input  A3,
  input  B0,
  input  B1,
  input  B2,
  input  in_8,
  output out_9,
  output out_10,
  output out_11,
  output out_12
);

  and and_1 (out_9, A0, B0);
  and and_2 (out_10, A1, B1);
  and and_3 (out_11, A2, B2);
  and and_4 (out_12, A3, in_8);

  // Notes on the sheet:
  //   AND
endmodule

// XOR
module \xor  (
  input  A0,
  input  A1,
  input  A2,
  input  A3,
  input  B0,
  input  B1,
  input  B2,
  input  B3,
  output out_9,
  output out_10,
  output out_11,
  output out_12
);

  xor xor_1 (out_9, A0, B0);
  xor xor_2 (out_10, A1, B1);
  xor xor_3 (out_11, A2, B2);
  xor xor_4 (out_12, A3, B3);

  // Notes on the sheet:
  //   XOR
endmodule

// S
module _1_bit_full_adder (
  input  A,
  input  B,
  input  C,
  output S,
  output CO
);

  wire and_1_out, and_2_out, and_3_out;

  ExactlyOne xor_1 (.out(S), .in0(A), .in1(B), .in2(C));
  and and_1 (and_1_out, A, B);
  and and_2 (and_2_out, B, C);
  and and_3 (and_3_out, A, C);
  or or_1 (CO, and_1_out, and_2_out, and_3_out);

  // Notes on the sheet:
  //   1-BIT FULL ADDER
endmodule
